# Fritzing sketch sketch (saved by Fritzing 1.0.6)
breadboards: 1

parts:
  Raspberry_Pi1 = Raspberry Pi B+
  Adafruit#1 = Adafruit ADS1115 16-Bit ADC [part_number=1085]
  KY-1 = KY-039 Heartbeat Sensor [part_number=KY-039]  # not connected
  KY-2 = KY-016 3-Color RGB LED Module [part_number="RGB Status LED"]
  KY-3 = KY-006 Passive Buzzer Module [part_number=KY-006]
  KY-5 = KY-001 DS18B20 Temperature Sensor [part_number=KY-001]
  AD1 = AD8232 ECG Module [part_number=AD8232]
  MAX1 = MAX30102 Pulse Oximeter [part_number=MAX30102]

nets:
  3V3: Raspberry_Pi1.3v3, Raspberry_Pi1.3V3, Adafruit#1.VCC, KY-3.NC, KY-5.+, AD1.3.3V, MAX1.VIN
  N1: Raspberry_Pi1.GPIO2, Adafruit#1.SDA, MAX1.SDA
  N2: Raspberry_Pi1.GPIO3, Adafruit#1.SCL, MAX1.SCL
  N3: Raspberry_Pi1.GPIO4, KY-5.S
  N4: Raspberry_Pi1.GPIO22, KY-2.R
  GND: Raspberry_Pi1.GND, Adafruit#1.GND, KY-2.-, KY-3.-, KY-5.-, AD1.GND, MAX1.GND
  N5: Raspberry_Pi1.GPIO8, AD1.LO-
  N6: Raspberry_Pi1.GPIO25, AD1.LO+
  N7: Raspberry_Pi1.GPIO24, KY-2.B
  N8: Raspberry_Pi1.GPIO23, KY-2.G
  N9: Raspberry_Pi1.GPIO18, KY-3.S
  N10: Adafruit#1.AIN0, AD1.OUTPUT

custom parts:
  KY-039 Heartbeat Sensor: KY-039 heartbeat/pulse sensor module commonly included in 37-in-1 sensor kits. Pin order is S, +, -.
  KY-016 3-Color RGB LED Module: KY-016 3-color RGB LED module. Common cathode pin is marked -; drive R, G, and B individually.
  KY-006 Passive Buzzer Module: KY-006 passive piezo buzzer module. Drive S with a square wave or tone output; the middle header pin is typically not connected; - is GND.
  KY-001 DS18B20 Temperature Sensor: KY-001 DS18B20 1-Wire digital temperature sensor module. Pin order is S, +, - on common Keyes-style modules; always confirm the silkscreen on your board.
  AD8232 ECG Module: AD8232 single-lead ECG (electrocardiogram) heart rate monitor module. Outputs an analog signal proportional to the ECG waveform. Includes lead-off detection outputs (LO+, LO-) and a shutdown pin (SDN). Connect RA, LA, and RL electrode snaps to the corresponding body leads.
  MAX30102 Pulse Oximeter: MAX30102 pulse oximeter and heart rate monitor module. Uses I2C (address 0x57) to report SpO2 and heart rate data. Integrated red (660 nm) and infrared (880 nm) LEDs with optical sensor. Supply voltage 1.8–5 V via VIN. INT is an active-low interrupt output.
